# Fritzing sketch Master_slave_setup (saved by Fritzing 0.9.10b)
breadboards: 1

parts:
  Mod1 = Amica NodeMCU DEVKIT 1.0
  Part1 = Arduino Uno (Rev3)
  Keypad4x2 = Keypad Membran 4x4

nets:
  N1: Mod1.pin1, Mod1.pin_10, Mod1.pin_26
  N2: Mod1.pin2, Mod1.pin_9, Mod1.pin_25, Mod1.pin_29, Part1.GND
  N3: Mod1.pin_11, Part1.A5/SCL
  N4: Mod1.pin_12, Part1.A4/SDA
  N5: Part1.D8, Keypad4x2.Pin6
  N6: Part1.D9_PWM, Keypad4x2.Pin5
  N7: Part1.D2, Keypad4x2.Pin4
  N8: Part1.D3_PWM, Keypad4x2.Pin3
  N9: Part1.D4, Keypad4x2.Pin2
  N10: Part1.D5_PWM, Keypad4x2.Pin1
  N11: Part1.D6_PWM, Keypad4x2.Pin8
  N12: Part1.D7, Keypad4x2.Pin7

custom parts:
  Keypad Membran 4x4: Membrane Keypad 4x4 Matrix
